# Fritzing sketch countdown (saved by Fritzing 0.9.3b)
circuit board: 0.6cm x 0.6cm
circuit board: 0.6cm x 0.6cm
circuit board: 0.6cm x 0.6cm
circuit board: 2.25cm x 3.29cm
circuit board: 2.25cm x 3.29cm
breadboards: 1

parts:
  U3 = IC, SIP package, 5 pins [chip_label=IC]
  U2 = IC, SIP package, 5 pins [chip_label=IC]
  U4 = SO16 [chip_label=TLC5916 package=SO]
  U6 = IC, SIP package, 7 pins [chip_label=IC]
  U7 = SO16 [chip_label=TLC5916 package=SO]
  J2 = female pin header, 8 pins [form="♀ (female)"]
  J3 = female pin header, 8 pins [form="♀ (female)"]
  J1 = female pin header, 4 pins [form="♀ (female)"]
  J4 = female pin header, 4 pins [form="♀ (female)"]
  J5 = female pin header, 4 pins [form="♀ (female)"]
  J6 = female pin header, 4 pins [form="♀ (female)"]
  R1 = Resistor [tolerance=±5% resistance=220 package=THT]
  D1 = Rectifier Diode [part_number=1N4001 package="300 mil [THT]"]
  U5 = IC, SIP package, 7 pins [chip_label=IC]

nets:
  N1: U3.pin1, U7.10
  N2: U3.pin2, U7.9
  N3: U3.pin3, J2.pin8, J3.pin8
  N4: U3.pin4, U7.8
  N5: U3.pin5, U7.7
  N6: U2.pin1, U7.6
  N7: U2.pin2, U7.5
  N8: U2.pin4, U7.12
  N9: U2.pin5, U7.11
  N10: U4.1, J1.pin4, J5.pin4, R1.Pin_0
  N11: U4.2, J4.pin2
  N12: U4.3, J4.pin1, J6.pin1
  N13: U4.4, J4.pin3, J6.pin3
  N14: U4.5, U6.pin6
  N15: U4.6, U6.pin4
  N16: U4.7, U6.pin3
  N17: U4.8, D1.cathode
  N18: U4.9, U6.pin1
  N19: U4.10, U5.pin7
  N20: U4.11, U5.pin2
  N21: U4.12, U5.pin1
  N22: U4.13, J4.pin4, J6.pin4
  N23: U4.14, J6.pin2
  N24: U4.15, R1.Pin_1
  N25: U4.16, J1.pin1, J5.pin1
  N26: U6.pin2, D1.anode
  N27: U6.pin7, J1.pin3, J5.pin3
  N28: U7.1, J2.pin2, J3.pin2
  N29: U7.2, J2.pin3
  N30: U7.3, J2.pin4, J3.pin4
  N31: U7.4, J2.pin5, J3.pin5
  N32: U7.13, J2.pin6, J3.pin6
  N33: U7.14, J3.pin3
  N34: U7.16, J2.pin1, J3.pin1
  N35: J1.pin2, J5.pin2

notes:
  Vdd
  GND
  Vled
  NC
